// Logisim project ALU32.circ as structural Verilog
module Add32 (
  input  [31:0] A,
  input  [31:0] B,
  input  Cin,
  output V,
  output [31:0] C
);

  wire add16_1_cout;

  Add16 add16_1 (.A(A[15:0]), .B(B[15:0]), .Cin(Cin), .Cout(add16_1_cout), .Sout(C[15:0]));
  Add16V add16v_1 (.A(A[31:16]), .B(B[31:16]), .Cin(add16_1_cout), .V(V), .Sout(C[31:16]));
endmodule

module LeftShift32 (
  input  [31:0] B,
  input  [4:0] Sa,
  input  Cin,
  output [31:0] C
);

  wire [0:0] bit_extender_5_out;
  wire [1:0] bit_extender_4_out;
  wire [3:0] bit_extender_3_out;
  wire [7:0] bit_extender_2_out;
  wire [15:0] bit_extender_1_out;
  wire [31:0] multiplexer_1_out, multiplexer_2_out, multiplexer_4_out;
  wire [31:2] multiplexer_3_out_2;
  wire [31:30] multiplexer_3_out;

  assign bit_extender_1_out = {{15{Cin}}, Cin};  // Bit_Extender bit_extender_1
  Multiplexer #(.width(32), .enable("false")) multiplexer_1 (
    .in0(B), .in1({B[15:0], bit_extender_1_out}), .out(multiplexer_1_out), .sel(Sa[4]));
  Bit_Extender #(.in_width(16), .out_width(8)) bit_extender_2 (.in(bit_extender_1_out), .out(bit_extender_2_out));
  Multiplexer #(.width(32), .enable("false")) multiplexer_2 (
    .in0(multiplexer_1_out), .in1({multiplexer_1_out[23:0], bit_extender_2_out}), .out(multiplexer_2_out),
    .sel(Sa[3]));
  Bit_Extender #(.out_width(4)) bit_extender_3 (.in(bit_extender_2_out), .out(bit_extender_3_out));
  Multiplexer #(.width(32), .enable("false")) multiplexer_3 (
    .in0(multiplexer_2_out), .in1({multiplexer_2_out[27:0], bit_extender_3_out}),
    .out({multiplexer_3_out, multiplexer_3_out_2}), .sel(Sa[2]));
  Bit_Extender #(.in_width(4), .out_width(2)) bit_extender_4 (.in(bit_extender_3_out), .out(bit_extender_4_out));
  Multiplexer #(.width(32), .enable("false")) multiplexer_4 (
    .in0({multiplexer_3_out, multiplexer_3_out_2}), .in1({multiplexer_3_out_2, bit_extender_4_out}),
    .out(multiplexer_4_out), .sel(Sa[1]));
  Bit_Extender #(.in_width(2), .out_width(1)) bit_extender_5 (.in(bit_extender_4_out), .out(bit_extender_5_out[0]));
  Multiplexer #(.width(32), .enable("false")) multiplexer_5 (
    .in0(multiplexer_4_out), .in1({multiplexer_4_out[30:0], bit_extender_5_out[0]}), .out(C), .sel(Sa[0]));
endmodule

module Add1 (
  input  A,
  input  B,
  input  Cin,
  output Sout,
  output Cout
);

  wire and_1_out, and_2_out, xor_1_out;

  xor xor_1 (xor_1_out, A, B);
  and and_1 (and_1_out, A, B);
  xor xor_2 (Sout, xor_1_out, Cin);
  and and_2 (and_2_out, xor_1_out, Cin);
  or or_1 (Cout, and_2_out, and_1_out);
endmodule

module Add2 (
  input  [1:0] A,
  input  [1:0] B,
  input  Cin,
  output Cout,
  output [1:0] Sout
);

  wire add1_1_cout;

  Add1 add1_1 (.A(A[0]), .B(B[0]), .Cin(Cin), .Sout(Sout[0]), .Cout(add1_1_cout));
  Add1 add1_2 (.A(A[1]), .B(B[1]), .Cin(add1_1_cout), .Sout(Sout[1]), .Cout(Cout));
endmodule

module Add2V (
  input  [1:0] A,
  input  [1:0] B,
  input  Cin,
  output V,
  output [1:0] Sout
);

  wire add1_1_cout, add1_2_cout;

  Add1 add1_1 (.A(A[0]), .B(B[0]), .Cin(Cin), .Sout(Sout[0]), .Cout(add1_1_cout));
  Add1 add1_2 (.A(A[1]), .B(B[1]), .Cin(add1_1_cout), .Sout(Sout[1]), .Cout(add1_2_cout));
  xor xor_1 (V, add1_2_cout, add1_1_cout);
endmodule

module Add4 (
  input  [3:0] A,
  input  [3:0] B,
  input  Cin,
  output Cout,
  output [3:0] Sout
);

  wire add2_1_cout;

  Add2 add2_1 (.A(A[1:0]), .B(B[1:0]), .Cin(Cin), .Cout(add2_1_cout), .Sout(Sout[1:0]));
  Add2 add2_2 (.A(A[3:2]), .B(B[3:2]), .Cin(add2_1_cout), .Cout(Cout), .Sout(Sout[3:2]));
endmodule

module Add4V (
  input  [3:0] A,
  input  [3:0] B,
  input  Cin,
  output V,
  output [3:0] Sout
);

  wire add2_1_cout;

  Add2 add2_1 (.A(A[1:0]), .B(B[1:0]), .Cin(Cin), .Cout(add2_1_cout), .Sout(Sout[1:0]));
  Add2V add2v_1 (.A(A[3:2]), .B(B[3:2]), .Cin(add2_1_cout), .V(V), .Sout(Sout[3:2]));
endmodule

module Add8 (
  input  [7:0] A,
  input  [7:0] B,
  input  Cin,
  output Cout,
  output [7:0] Sout
);

  wire add4_1_cout;

  Add4 add4_1 (.A(A[3:0]), .B(B[3:0]), .Cin(Cin), .Cout(add4_1_cout), .Sout(Sout[3:0]));
  Add4 add4_2 (.A(A[7:4]), .B(B[7:4]), .Cin(add4_1_cout), .Cout(Cout), .Sout(Sout[7:4]));
endmodule

module Add8V (
  input  [7:0] A,
  input  [7:0] B,
  input  Cin,
  output V,
  output [7:0] Sout
);

  wire add4_1_cout;

  Add4 add4_1 (.A(A[3:0]), .B(B[3:0]), .Cin(Cin), .Cout(add4_1_cout), .Sout(Sout[3:0]));
  Add4V add4v_1 (.A(A[7:4]), .B(B[7:4]), .Cin(add4_1_cout), .V(V), .Sout(Sout[7:4]));
endmodule

module Add16 (
  input  [15:0] A,
  input  [15:0] B,
  input  Cin,
  output Cout,
  output [15:0] Sout
);

  wire add8_1_cout;

  Add8 add8_1 (.A(A[7:0]), .B(B[7:0]), .Cin(Cin), .Cout(add8_1_cout), .Sout(Sout[7:0]));
  Add8 add8_2 (.A(A[15:8]), .B(B[15:8]), .Cin(add8_1_cout), .Cout(Cout), .Sout(Sout[15:8]));
endmodule

module Add16V (
  input  [15:0] A,
  input  [15:0] B,
  input  Cin,
  output V,
  output [15:0] Sout
);

  wire add8_1_cout;

  Add8 add8_1 (.A(A[7:0]), .B(B[7:0]), .Cin(Cin), .Cout(add8_1_cout), .Sout(Sout[7:0]));
  Add8V add8v_1 (.A(A[15:8]), .B(B[15:8]), .Cin(add8_1_cout), .V(V), .Sout(Sout[15:8]));
endmodule

module GateOp (
  input  [31:0] A,
  input  [31:0] B,
  input  [3:0] Op,
  output [31:0] C
);

  wire and_2_out, and_3_out, or_2_out;
  wire [31:0] and_1_out, nor_1_out, or_1_out, xor_1_out;

  assign and_1_out = A & B;  // AND_Gate and_1, 32 bits wide
  assign or_1_out = A | B;  // OR_Gate or_1, 32 bits wide
  assign xor_1_out = A ^ B;  // XOR_Gate xor_1, 32 bits wide
  assign nor_1_out = ~(A | B);  // NOR_Gate nor_1, 32 bits wide
  and and_2 (and_2_out, Op[1], ~Op[2], Op[3]);  // AND_Gate
  and and_3 (and_3_out, ~Op[1], Op[2], ~Op[3]);  // AND_Gate
  or or_2 (or_2_out, and_2_out, and_3_out);
  Multiplexer #(.select(2), .width(32)) multiplexer_1 (
    .in0(and_1_out), .in1(or_1_out), .in2(xor_1_out), .in3(nor_1_out), .out(C), .sel(Op[1:0]), .en(or_2_out));
endmodule

module Mirror (
  input  [31:0] B,
  output [31:0] B_Reverse,
  output SignBit
);


  assign B_Reverse = {B[0], B[1], B[2], B[3], B[4], B[5], B[6], B[7], B[8], B[9], B[10], B[11], B[12], B[13], B[14], B[15], B[16], B[17], B[18], B[19], B[20], B[21], B[22], B[23], B[24], B[25], B[26], B[27], B[28], B[29], B[30], B[31]};
  assign SignBit = B[31];
endmodule
