// Logisim project Add32.circ as structural Verilog
module OneBitAdder (
  input  A,
  input  B,
  input  Cin,
  output S,
  output Cout
);

  wire and_1_out, and_2_out, xor_1_out;

  xor xor_1 (xor_1_out, A, B);
  and and_1 (and_1_out, A, B);
  xor xor_2 (S, xor_1_out, Cin);
  and and_2 (and_2_out, xor_1_out, Cin);
  or or_1 (Cout, and_2_out, and_1_out);
endmodule

module FourBitAdder (
  input  [3:0] A,
  input  [3:0] B,
  input  Cin,
  output Cout,
  output V,
  output [3:0] S
);

  wire onebitadder_1_cout, onebitadder_2_cout, onebitadder_3_cout;

  OneBitAdder onebitadder_1 (.A(A[0]), .B(B[0]), .Cin(Cin), .S(S[0]), .Cout(onebitadder_1_cout));
  OneBitAdder onebitadder_2 (.A(A[1]), .B(B[1]), .Cin(onebitadder_1_cout), .S(S[1]), .Cout(onebitadder_2_cout));
  OneBitAdder onebitadder_3 (.A(A[2]), .B(B[2]), .Cin(onebitadder_2_cout), .S(S[2]), .Cout(onebitadder_3_cout));
  OneBitAdder onebitadder_4 (.A(A[3]), .B(B[3]), .Cin(onebitadder_3_cout), .S(S[3]), .Cout(Cout));
  xor xor_1 (V, Cout, onebitadder_3_cout);
endmodule

module SixteenBitAdder (
  input  [15:0] A,
  input  [15:0] B,
  input  Cin,
  output Cout,
  output V,
  output [15:0] S
);

  wire fourbitadder_1_cout, fourbitadder_2_cout, fourbitadder_3_cout;

  FourBitAdder fourbitadder_1 (.A(A[3:0]), .B(B[3:0]), .Cin(Cin), .Cout(fourbitadder_1_cout), .S(S[3:0]));  // open: V
  FourBitAdder fourbitadder_2 (
    .A(A[7:4]), .B(B[7:4]), .Cin(fourbitadder_1_cout), .Cout(fourbitadder_2_cout), .S(S[7:4]));  // open: V
  FourBitAdder fourbitadder_3 (
    .A(A[11:8]), .B(B[11:8]), .Cin(fourbitadder_2_cout), .Cout(fourbitadder_3_cout), .S(S[11:8]));  // open: V
  FourBitAdder fourbitadder_4 (.A(A[15:12]), .B(B[15:12]), .Cin(fourbitadder_3_cout), .Cout(Cout), .V(V), .S(S[15:12]));
endmodule

module ThirtyTwoBitAdder (
  input  [31:0] A,
  input  [31:0] B,
  input  Cin,
  output Cout,
  output V,
  output [31:0] S
);

  wire sixteenbitadder_1_cout;

  SixteenBitAdder sixteenbitadder_1 (
    .A(A[15:0]), .B(B[15:0]), .Cin(Cin), .Cout(sixteenbitadder_1_cout), .S(S[15:0]));  // open: V
  SixteenBitAdder sixteenbitadder_2 (
    .A(A[31:16]), .B(B[31:16]), .Cin(sixteenbitadder_1_cout), .Cout(Cout), .V(V), .S(S[31:16]));
endmodule
